# Fritzing sketch Fritzing (saved by Fritzing 0.9.10b)
perfboards: 1

parts:
  J1 = screw terminal, 4 pins  # not connected
  M1 = RioRand LM2596  # not connected
  Componente1 = Arduino Uno (Rev3)
  RHT1 = Humidity and Temperature Sensor RHT03
  LED1 = LED - 5mm [color="Red (633nm)" current=0.030 package="5 mm [THT]"]
  R1 = Resistor [tolerance=±5% power=0.25 resistance=220 package=THT]
  S1 = Pushbutton [package="[THT]"]
  WeMos_D1_Mini_Relay_Shield_V1 = WeMos D1 Mini Relay Shield V2
  GSM_SIM_GPSR_SMS_SIM900_SIM1 = SIM800L [package=THT]

nets:
  N1: Componente1.D2, GSM_SIM_GPSR_SMS_SIM900_SIM1.SIM_TXD
  N2: Componente1.D3_PWM, GSM_SIM_GPSR_SMS_SIM900_SIM1.SIM_RXD
  N3: Componente1.D4, WeMos_D1_Mini_Relay_Shield_V1.D1
  N4: Componente1.D5_PWM, RHT1.Data-signal
  N5: Componente1.D6_PWM, LED1.cathode
  N6: Componente1.D7, Componente1.3V3, S1.Pin_3, S1.Pin_4
  5V: Componente1.5V, RHT1.Vcc
  N7: Componente1.GND, RHT1.GND_1, R1.Pin_1

notes:
  Here 6V 2100mA
